# Fritzing sketch Wumpus_Board (saved by Fritzing 0.9.3b)
circuit board: 7.59249cm x 9.97991cm
breadboards: 1

parts:
  J2 = female pin header, 2 pins [form="♀ (female)"]  # not connected
  J3 = female pin header, 2 pins [form="♀ (female)"]
  J4 = female pin header, 3 pins [form="♀ (female)"]
  J1 = female pin header, 4 pins [form="♀ (female)"]
  D1 = Rectifier Diode [part_number=1N4001 package="300 mil [THT]"]
  J5 = female pin header, 1 pin [form="♀ (female)"]
  J6 = female pin header, 1 pin [form="♀ (female)"]  # not connected
  J7 = female pin header, 1 pin [form="♀ (female)"]
  J8 = female pin header, 1 pin [form="♀ (female)"]
  J9 = female pin header, 1 pin [form="♀ (female)"]  # not connected
  J10 = female pin header, 1 pin [form="♀ (female)"]
  Pad11 = Pad [width=3.3349889630383629 height=1.5878834494179259 connect=center]
  Pad12 = Pad [width=3.3349889630383629 height=1.5878834494179259 connect=center]
  Pad13 = Pad [width=3.3349889630383629 height=1.5878834494179259 connect=center]
  S3 = SPST Switch [package=switch-spdt_lock.007s]
  VCC1 = Battery

nets:
  N1: J3.pin1, J7.pin1, J10.pin1, VCC1.-
  N2: J4.pin1, D1.anode, S3.S
  N3: J4.pin2, Pad12.pad
  N4: J1.pin2, J8.pin1
  N5: J1.pin3, J5.pin1
  N6: J1.pin4, Pad13.pad
  N7: D1.cathode, Pad11.pad
  N8: S3.P, VCC1.+

notes:
  -
  <--bar
  --> Note Arrow Direction -->
  [USB]
  sponsored by
  hardware project
  diode
  battery
  red
  black
  power switch
  STM32 Blue Pill
  attach battery here
